# Fritzing sketch BME280onlyV06 (saved by Fritzing 0.9.3b)
circuit board: 5.5cm x 5.7cm
breadboards: 1

parts:
  D2 = LED - 3mm [color="Red (633nm)" package="3 mm [THT]"]
  IC1 = Header 4 [part_number=DS3231 package=molex-1x4_lock]
  Raspberry_Pi_3 = Raspberry Pi 3 [part_number=RPI-3-V1.2]
  R1 = Resistor [tolerance=±5% resistance=1k package="1206 [SMD]"]
  R9 = Resistor [tolerance=±5% resistance=1k package=THT]

nets:
  N1: D2.cathode, Raspberry_Pi_3.GPIO17
  N2: D2.anode, R1.Pin_0, R9.Pin_0
  N3: IC1.1, Raspberry_Pi_3.GND
  3V3: IC1.2, Raspberry_Pi_3.3v3, Raspberry_Pi_3.3V3
  3.3V SDA: IC1.3, Raspberry_Pi_3.GPIO2
  3.3V SCL: IC1.4, Raspberry_Pi_3.GPIO3
  N4: Raspberry_Pi_3.GPIO18, R1.Pin_1, R9.Pin_1

notes:
  BME
  GND
  3.3V
  SDA
  SCL
  Your Name
  BME280onlyV06
