# Fritzing sketch SimpleBMERTCv00 (saved by Fritzing 0.9.3b)
circuit board: 1.76054cm x 2.74344cm
breadboards: 1

parts:
  J1 = double row female pin header, 6 pins [form="♀ (female)"]
  J2 = female pin header, 4 pins [form="♀ (female)"]

nets:
  N1: J1.pin1, J2.pin2
  N2: J1.pin2, J2.pin3
  N3: J1.pin3, J2.pin4
  N4: J1.pin4, J2.pin1

notes:
  SDA
  RTC
  Your Name
  RPi
  GND
  3v3
  SCL
  BME
